// Logisim project basic.circ as structural Verilog: 4 circuits, main circuit 16-bit ALU
module _16_bit_ALU (
  input  [15:0] in_1,
  input  [15:0] in_2,
  input  [1:0] ALU_OP,
  output [15:0] out_4
);

  wire and_1_out;
  wire [15:0] adder_1_out, and_2_out, multiplexer_1_out, not_1_out, or_1_out;

  Multiplexer #(.width(16), .enable("false")) multiplexer_1 (
    .in0(in_2), .in1(not_1_out), .out(multiplexer_1_out), .sel(and_1_out));
  assign not_1_out = ~in_2;  // NOT_Gate not_1, 16 bits wide
  Adder #(.width(16)) adder_1 (.a(in_1), .b(multiplexer_1_out), .out(adder_1_out), .cin(and_1_out));  // open: cout
  and and_1 (and_1_out, ALU_OP[0], ALU_OP[1]);
  assign and_2_out = multiplexer_1_out & in_1;  // AND_Gate and_2, 16 bits wide
  assign or_1_out = multiplexer_1_out | in_1;  // OR_Gate or_1, 16 bits wide
  Multiplexer #(.select(2), .width(16), .enable("false")) multiplexer_2 (
    .in0(adder_1_out), .in1(and_2_out), .in2(or_1_out), .in3(adder_1_out), .out(out_4), .sel(ALU_OP));

  // Notes on the sheet:
  //   A
  //   B
  //   OUT
endmodule

module _16x16_bit_Register_File (
  input  [15:0] d_in,
  input  [3:0] ra1,
  input  En,
  input  [3:0] _4,
  input  [3:0] ra2,
  input  clk,
  output [15:0] out1,
  output [15:0] out2
);

  wire demultiplexer_1_out0, demultiplexer_1_out1, demultiplexer_1_out2, demultiplexer_1_out3,
       demultiplexer_1_out4, demultiplexer_1_out5, demultiplexer_1_out6, demultiplexer_1_out7,
       demultiplexer_1_out8, demultiplexer_1_out9, demultiplexer_1_out10, demultiplexer_1_out11,
       demultiplexer_1_out12, demultiplexer_1_out13, demultiplexer_1_out14, demultiplexer_1_out15;
  wire [15:0] register_1_q, register_2_q, register_3_q, register_4_q, register_5_q, register_6_q,
       register_7_q, register_8_q, register_9_q, register_10_q, register_11_q, register_12_q, register_13_q,
       register_14_q, register_15_q, register_16_q;

  Demultiplexer #(.select(4), .enable("false")) demultiplexer_1 (
    .out0(demultiplexer_1_out0), .out1(demultiplexer_1_out1), .out2(demultiplexer_1_out2),
    .out3(demultiplexer_1_out3), .out4(demultiplexer_1_out4), .out5(demultiplexer_1_out5),
    .out6(demultiplexer_1_out6), .out7(demultiplexer_1_out7), .out8(demultiplexer_1_out8),
    .out9(demultiplexer_1_out9), .out10(demultiplexer_1_out10), .out11(demultiplexer_1_out11),
    .out12(demultiplexer_1_out12), .out13(demultiplexer_1_out13), .out14(demultiplexer_1_out14),
    .out15(demultiplexer_1_out15), .in(En), .sel(_4));
  Register #(.width(16)) register_1 (.D(d_in), .en(demultiplexer_1_out0), .Q(register_1_q), .clk(clk));  // open: clr
  Register #(.width(16)) register_2 (.D(d_in), .en(demultiplexer_1_out2), .Q(register_2_q), .clk(clk));  // open: clr
  Register #(.width(16)) register_3 (.D(d_in), .en(demultiplexer_1_out4), .Q(register_3_q), .clk(clk));  // open: clr
  Register #(.width(16)) register_4 (.D(d_in), .en(demultiplexer_1_out6), .Q(register_4_q), .clk(clk));  // open: clr
  Register #(.width(16)) register_5 (.D(d_in), .en(demultiplexer_1_out8), .Q(register_5_q), .clk(clk));  // open: clr
  Register #(.width(16)) register_6 (.D(d_in), .en(demultiplexer_1_out10), .Q(register_6_q), .clk(clk));  // open: clr
  Register #(.width(16)) register_7 (.D(d_in), .en(demultiplexer_1_out12), .Q(register_7_q), .clk(clk));  // open: clr
  Register #(.width(16)) register_8 (.D(d_in), .en(demultiplexer_1_out14), .Q(register_8_q), .clk(clk));  // open: clr
  Register #(.width(16)) register_9 (.D(d_in), .en(demultiplexer_1_out1), .Q(register_9_q), .clk(clk));  // open: clr
  Register #(.width(16)) register_10 (.D(d_in), .en(demultiplexer_1_out3), .Q(register_10_q), .clk(clk));  // open: clr
  Register #(.width(16)) register_11 (.D(d_in), .en(demultiplexer_1_out5), .Q(register_11_q), .clk(clk));  // open: clr
  Register #(.width(16)) register_12 (.D(d_in), .en(demultiplexer_1_out7), .Q(register_12_q), .clk(clk));  // open: clr
  Register #(.width(16)) register_13 (.D(d_in), .en(demultiplexer_1_out9), .Q(register_13_q), .clk(clk));  // open: clr
  Register #(.width(16)) register_14 (.D(d_in), .en(demultiplexer_1_out11), .Q(register_14_q), .clk(clk));  // open: clr
  Register #(.width(16)) register_15 (.D(d_in), .en(demultiplexer_1_out13), .Q(register_15_q), .clk(clk));  // open: clr
  Register #(.width(16)) register_16 (.D(d_in), .en(demultiplexer_1_out15), .Q(register_16_q), .clk(clk));  // open: clr
  Multiplexer #(.select(4), .width(16), .enable("false")) multiplexer_1 (
    .in0(register_1_q), .in1(register_9_q), .in2(register_2_q), .in3(register_10_q), .in4(register_3_q),
    .in5(register_11_q), .in6(register_4_q), .in7(register_12_q), .in8(register_5_q), .in9(register_13_q),
    .in10(register_6_q), .in11(register_14_q), .in12(register_7_q), .in13(register_15_q),
    .in14(register_8_q), .in15(register_16_q), .out(out1), .sel(ra1));
  Multiplexer #(.select(4), .width(16), .enable("false")) multiplexer_2 (
    .in0(register_1_q), .in1(register_9_q), .in2(register_2_q), .in3(register_10_q), .in4(register_3_q),
    .in5(register_11_q), .in6(register_4_q), .in7(register_12_q), .in8(register_5_q), .in9(register_13_q),
    .in10(register_6_q), .in11(register_14_q), .in12(register_7_q), .in13(register_15_q),
    .in14(register_8_q), .in15(register_16_q), .out(out2), .sel(ra2));
endmodule

module Full_Cpu (
  input  pc_rst,
  input  clk
);

  wire D2_sel, D_sel, not_1_out, RA2_sel;
  wire [1:0] op;
  wire [3:0] multiplexer_1_out;
  wire [15:0] bit_extender_1_out, counter_1_q, multiplexer_2_out, multiplexer_3_out, n16_bit_alu_1_out_4,
       n16x16_bit_register_file_1_out1, n16x16_bit_register_file_1_out2, ram_1_data, ram_2_data;

  Counter #(.width(16), .max('hffff)) counter_1 (
    .load(1'b0), .D(counter_1_q), .count(1'b1), .Q(counter_1_q), .clk(clk), .clr(pc_rst));  // open: carry
  RAM #(.addrWidth(16), .dataWidth(16)) ram_1 (.addr(counter_1_q), .data(ram_1_data), .clk(clk));  // open: sel, ld, clr
  CLU clu_1 (.inp(ram_1_data[15:12]), .op(op), .imm(D2_sel), .lw(D_sel), .sw(RA2_sel));
  _16x16_bit_Register_File u_16x16_bit_register_file_1 (
    .d_in(multiplexer_2_out), .En(not_1_out), .clk(clk), .out1(n16x16_bit_register_file_1_out1),
    .out2(n16x16_bit_register_file_1_out2), ._4(ram_1_data[11:8]), .ra1(ram_1_data[7:4]),
    .ra2(multiplexer_1_out));
  Multiplexer #(.width(4), .enable("false")) multiplexer_1 (
    .in0(ram_1_data[3:0]), .in1(ram_1_data[11:8]), .out(multiplexer_1_out), .sel(RA2_sel));
  not not_1 (not_1_out, RA2_sel);
  Multiplexer #(.width(16), .enable("false")) multiplexer_2 (
    .in0(n16_bit_alu_1_out_4), .in1(ram_2_data), .out(multiplexer_2_out), .sel(D_sel));
  assign bit_extender_1_out = {{12{ram_1_data[3]}}, ram_1_data[3:0]};  // Bit_Extender bit_extender_1
  _16_bit_ALU u_16_bit_alu_1 (
    .in_1(n16x16_bit_register_file_1_out1), .in_2(multiplexer_3_out), .out_4(n16_bit_alu_1_out_4), .ALU_OP(op));
  Multiplexer #(.width(16), .enable("false")) multiplexer_3 (
    .in0(n16x16_bit_register_file_1_out2), .in1(bit_extender_1_out), .out(multiplexer_3_out), .sel(D2_sel));
  // Probe on n16_bit_alu_1_out_4
  RAM #(.addrWidth(16), .dataWidth(16), .bus("separate")) ram_2 (
    .addr(n16_bit_alu_1_out_4), .din(n16x16_bit_register_file_1_out2), .data(ram_2_data), .str(RA2_sel),
    .sel(1'b1), .clk(clk), .ld(D_sel), .clr(1'b0));
endmodule

module CLU (
  input  [3:0] inp,
  output [1:0] op,
  output imm,
  output lw,
  output sw
);

  or or_1 (imm, inp[2], inp[3]);
  and and_1 (lw, ~inp[3], inp[2]);  // AND_Gate
  and and_2 (sw, ~inp[2], inp[3]);  // AND_Gate

  assign op = inp[1:0];
endmodule
