// Logisim project upgraded.circ as structural Verilog: 11 circuits, main circuit 16-bit ALU
module Full_Cpu (
  input  PC_rst,
  input  clk
);

  wire alu_zero, and_1_out, and_2_out, clu_1_rf_en, D1_sel, D_sel, PCb_sel, PCbeq, PCbne, PCj_sel, Ra1_sel;
  wire [2:0] op;
  wire [3:0] multiplexer_3_out;
  wire [15:0] imm, multiplexer_4_out, multiplexer_5_out, n16_bit_alu_1_out_4, n16x16b_reg_file_1_d1,
       n16x16b_reg_file_1_d2, ram_2_data;
  wire [17:0] adder_1_out, adder_2_out, bit_extender_1_out, multiplexer_1_out, multiplexer_2_out, ram_1_data,
       register_1_q;
  wire [20:18] ram_1_data_2;

  assign bit_extender_1_out = {{2{imm[15]}}, imm};  // Bit_Extender bit_extender_1
  Adder #(.width(18)) adder_1 (.a({18{1'b0}}), .b(register_1_q), .out(adder_1_out), .cin(1'b1));  // open: cout
  Adder #(.width(18)) adder_2 (.a(bit_extender_1_out), .b(adder_1_out), .out(adder_2_out), .cin(1'b0));  // open: cout
  Multiplexer #(.width(18), .enable("false")) multiplexer_1 (
    .in0(adder_1_out), .in1(adder_2_out), .out(multiplexer_1_out), .sel(PCb_sel));
  Multiplexer #(.width(18), .enable("false")) multiplexer_2 (
    .in0(multiplexer_1_out), .in1(ram_1_data), .out(multiplexer_2_out), .sel(PCj_sel));
  Register #(.width(18)) register_1 (.D(multiplexer_2_out), .en(1'b1), .Q(register_1_q), .clk(clk), .clr(PC_rst));
  RAM #(.addrWidth(18), .dataWidth(21)) ram_1 (
    .addr(register_1_q), .data({ram_1_data_2, ram_1_data}), .clk(clk));  // open: sel, ld, clr
  CLU clu_1 (
    .inp({ram_1_data_2, ram_1_data[17:15]}), .op(op), .D1_sel(D1_sel), .D_sel(D_sel), .Ra1_sel(Ra1_sel),
    .PCj_sel(PCj_sel), .PCbeq_sel(PCbeq), .PCbne_sel(PCbne), .RF_en(clu_1_rf_en));
  and and_1 (and_1_out, PCbeq, alu_zero);
  and and_2 (and_2_out, PCbne, ~alu_zero);  // AND_Gate
  Multiplexer #(.width(4), .enable("false")) multiplexer_3 (
    .in0(ram_1_data[6:3]), .in1(ram_1_data[14:11]), .out(multiplexer_3_out), .sel(Ra1_sel));
  or or_1 (PCb_sel, and_1_out, and_2_out);
  _16x16b_Reg_File u_16x16b_reg_file_1 (
    .Din(multiplexer_4_out), .en(clu_1_rf_en), .clk(clk), .D2(n16x16b_reg_file_1_d2),
    .D1(n16x16b_reg_file_1_d1), .Wa(ram_1_data[14:11]), .Ra0(ram_1_data[10:7]), .Ra1(multiplexer_3_out));
  Multiplexer #(.width(16), .enable("false")) multiplexer_4 (
    .in0(n16_bit_alu_1_out_4), .in1(ram_2_data), .out(multiplexer_4_out), .sel(D_sel));
  assign imm = {{9{ram_1_data[6]}}, ram_1_data[6:0]};  // Bit_Extender bit_extender_2
  _16_bit_ALU u_16_bit_alu_1 (
    .in_1(n16x16b_reg_file_1_d2), .in_2(multiplexer_5_out), .out_4(n16_bit_alu_1_out_4), .ALU_OP(op),
    .zero(alu_zero));
  Multiplexer #(.width(16), .enable("false")) multiplexer_5 (
    .in0(n16x16b_reg_file_1_d1), .in1(imm), .out(multiplexer_5_out), .sel(D1_sel));
  // Probe on n16_bit_alu_1_out_4
  RAM #(.addrWidth(16), .dataWidth(16), .bus("separate")) ram_2 (
    .addr(n16_bit_alu_1_out_4), .din(n16x16b_reg_file_1_d1), .data(ram_2_data), .str(Ra1_sel), .sel(1'b1),
    .clk(clk), .ld(D_sel), .clr(1'b0));
endmodule

module CLU (
  input  [5:0] inp,
  output [2:0] op,
  output D1_sel,
  output D_sel,
  output Ra1_sel,
  output PCbeq_sel,
  output PCbne_sel,
  output PCj_sel,
  output RF_en
);

  wire and_2_out, or_1_out, or_2_out;

  or or_1 (or_1_out, inp[3], inp[4], inp[5]);
  and and_1 (D_sel, inp[3], ~inp[4], ~inp[5]);  // AND_Gate
  and and_2 (and_2_out, ~inp[3], inp[4], ~inp[5]);  // AND_Gate
  and and_3 (PCbeq_sel, inp[3], ~inp[4], inp[5]);  // AND_Gate
  and and_4 (PCbne_sel, ~inp[3], inp[4], inp[5]);  // AND_Gate
  and and_5 (PCj_sel, ~inp[3], ~inp[4], inp[5]);  // AND_Gate
  nor nor_1 (RF_en, and_2_out, PCbeq_sel, PCbne_sel, PCj_sel);
  and and_6 (D1_sel, or_1_out, ~or_2_out);  // AND_Gate
  or or_2 (or_2_out, PCbeq_sel, PCbne_sel);
  or or_3 (Ra1_sel, PCbeq_sel, and_2_out, PCbne_sel);

  assign op = inp[2:0];
endmodule

module _16_bit_ALU (
  input  [15:0] in_1,
  input  [15:0] in_2,
  input  [2:0] ALU_OP,
  output [15:0] out_4,
  output zero
);

  wire and_1_out, n16b_comparator_1_lt_out;
  wire [15:0] adder_1_out, and_2_out, bit_extender_1_out, multiplexer_1_out, not_1_out, or_1_out;

  Multiplexer #(.width(16), .enable("false")) multiplexer_1 (
    .in0(in_2), .in1(not_1_out), .out(multiplexer_1_out), .sel(and_1_out));
  assign not_1_out = ~in_2;  // NOT_Gate not_1, 16 bits wide
  Adder #(.width(16)) adder_1 (.a(in_1), .b(multiplexer_1_out), .out(adder_1_out), .cin(and_1_out));  // open: cout
  and and_1 (and_1_out, ALU_OP[0], ALU_OP[1], ~ALU_OP[2]);  // AND_Gate
  assign bit_extender_1_out = {{15{1'b0}}, n16b_comparator_1_lt_out};  // Bit_Extender bit_extender_1
  assign and_2_out = multiplexer_1_out & in_1;  // AND_Gate and_2, 16 bits wide
  assign or_1_out = multiplexer_1_out | in_1;  // OR_Gate or_1, 16 bits wide
  _16b_Comparator u_16b_comparator_1 (
    .A({in_2[15], in_1[14:0]}), .B({in_1[15], in_2[14:0]}), .lt_in(1'b0), .eq_in(1'b1),
    .lt_out(n16b_comparator_1_lt_out));  // open: eq_out
  Multiplexer #(.select(3), .width(16), .enable("false")) multiplexer_2 (
    .in0(adder_1_out), .in1(and_2_out), .in2(or_1_out), .in3(adder_1_out), .in6(bit_extender_1_out),
    .out(out_4), .sel(ALU_OP));  // open: in4, in5, in7
  nor nor_1 (zero, out_4[0], out_4[1], out_4[2], out_4[3], out_4[4], out_4[5], out_4[6], out_4[7], out_4[8], out_4[9], out_4[10], out_4[11], out_4[12], out_4[13], out_4[14], out_4[15]);

  // Notes on the sheet:
  //   A
  //   B
  //   OUT
endmodule

module _32x16_bit_Register_File (
  input  [15:0] Din,
  input  en,
  input  [4:0] Ra0,
  input  [4:0] Ra1,
  input  [4:0] Wa,
  input  clk,
  output [15:0] D2,
  output [15:0] D1
);

  wire demultiplexer_1_out0, demultiplexer_1_out1;
  wire [15:0] n16x16b_reg_file_1_d1, n16x16b_reg_file_1_d2, n16x16b_reg_file_2_d1, n16x16b_reg_file_2_d2;

  Demultiplexer #(.enable("false")) demultiplexer_1 (
    .out0(demultiplexer_1_out0), .out1(demultiplexer_1_out1), .in(en), .sel(Wa[4]));
  _16x16b_Reg_File u_16x16b_reg_file_1 (
    .Din(Din), .en(demultiplexer_1_out0), .clk(clk), .D2(n16x16b_reg_file_1_d2), .D1(n16x16b_reg_file_1_d1),
    .Wa(Wa[3:0]), .Ra0(Ra0[3:0]), .Ra1(Ra1[3:0]));
  _16x16b_Reg_File u_16x16b_reg_file_2 (
    .Din(Din), .en(demultiplexer_1_out1), .clk(clk), .D2(n16x16b_reg_file_2_d2), .D1(n16x16b_reg_file_2_d1),
    .Wa(Wa[3:0]), .Ra0(Ra0[3:0]), .Ra1(Ra1[3:0]));
  Multiplexer #(.width(16), .enable("false")) multiplexer_1 (
    .in0(n16x16b_reg_file_1_d2), .in1(n16x16b_reg_file_2_d2), .out(D2), .sel(Ra0[4]));
  Multiplexer #(.width(16), .enable("false")) multiplexer_2 (
    .in0(n16x16b_reg_file_1_d1), .in1(n16x16b_reg_file_2_d1), .out(D1), .sel(Ra1[4]));

  // Other names for the same wires on the sheet: Ra0_t[3:0] = Ra0[3:0]; Ra1_t[3:0] = Ra1[3:0]; Wa_t[3:0] = Wa[3:0]
endmodule

module _16x16b_Reg_File (
  input  [15:0] Din,
  input  en,
  input  [3:0] Ra0,
  input  [3:0] Wa,
  input  clk,
  input  [3:0] Ra1,
  output [15:0] D2,
  output [15:0] D1
);

  wire demultiplexer_1_out0, demultiplexer_1_out1, demultiplexer_1_out2, demultiplexer_1_out3;
  wire [15:0] n4x16b_reg_file_1_d1, n4x16b_reg_file_1_d2, n4x16b_reg_file_2_d1, n4x16b_reg_file_2_d2,
       n4x16b_reg_file_3_d1, n4x16b_reg_file_3_d2, n4x16b_reg_file_4_d1, n4x16b_reg_file_4_d2;

  Demultiplexer #(.select(2), .enable("false")) demultiplexer_1 (
    .out0(demultiplexer_1_out0), .out1(demultiplexer_1_out1), .out2(demultiplexer_1_out2),
    .out3(demultiplexer_1_out3), .in(en), .sel(Wa[3:2]));
  _4x16b_Reg_File u_4x16b_reg_file_1 (
    .Din(Din), .en(demultiplexer_1_out0), .D2(n4x16b_reg_file_1_d2), .D1(n4x16b_reg_file_1_d1), .Wa(Wa[1:0]),
    .Ra0(Ra0[1:0]), .Ra1(Ra1[1:0]), .clk(clk));
  _4x16b_Reg_File u_4x16b_reg_file_2 (
    .Din(Din), .en(demultiplexer_1_out1), .D2(n4x16b_reg_file_2_d2), .D1(n4x16b_reg_file_2_d1), .Wa(Wa[1:0]),
    .Ra0(Ra0[1:0]), .Ra1(Ra1[1:0]), .clk(clk));
  _4x16b_Reg_File u_4x16b_reg_file_3 (
    .Din(Din), .en(demultiplexer_1_out2), .D2(n4x16b_reg_file_3_d2), .D1(n4x16b_reg_file_3_d1), .Wa(Wa[1:0]),
    .Ra0(Ra0[1:0]), .Ra1(Ra1[1:0]), .clk(clk));
  _4x16b_Reg_File u_4x16b_reg_file_4 (
    .Din(Din), .en(demultiplexer_1_out3), .D2(n4x16b_reg_file_4_d2), .D1(n4x16b_reg_file_4_d1), .Wa(Wa[1:0]),
    .Ra0(Ra0[1:0]), .Ra1(Ra1[1:0]), .clk(clk));
  Multiplexer #(.select(2), .width(16), .enable("false")) multiplexer_1 (
    .in0(n4x16b_reg_file_1_d2), .in1(n4x16b_reg_file_2_d2), .in2(n4x16b_reg_file_3_d2),
    .in3(n4x16b_reg_file_4_d2), .out(D2), .sel(Ra0[3:2]));
  Multiplexer #(.select(2), .width(16), .enable("false")) multiplexer_2 (
    .in0(n4x16b_reg_file_1_d1), .in1(n4x16b_reg_file_2_d1), .in2(n4x16b_reg_file_3_d1),
    .in3(n4x16b_reg_file_4_d1), .out(D1), .sel(Ra1[3:2]));

  // Other names for the same wires on the sheet: Ra0_t[1:0] = Ra0[1:0]; Ra1_t[1:0] = Ra1[1:0]; Wa_t[1:0] = Wa[1:0]
endmodule

module _4x16b_Reg_File (
  input  [15:0] Din,
  input  en,
  input  [1:0] Ra0,
  input  [1:0] Wa,
  input  clk,
  input  [1:0] Ra1,
  output [15:0] D2,
  output [15:0] D1
);

  wire demultiplexer_1_out0, demultiplexer_1_out1, demultiplexer_1_out2, demultiplexer_1_out3;
  wire [15:0] register_1_q, register_2_q, register_3_q, register_4_q;

  Demultiplexer #(.select(2), .enable("false")) demultiplexer_1 (
    .out0(demultiplexer_1_out0), .out1(demultiplexer_1_out1), .out2(demultiplexer_1_out2),
    .out3(demultiplexer_1_out3), .in(en), .sel(Wa));
  Register #(.width(16)) register_1 (.D(Din), .en(demultiplexer_1_out0), .Q(register_1_q), .clk(clk));  // open: clr
  Register #(.width(16)) register_2 (.D(Din), .en(demultiplexer_1_out1), .Q(register_2_q), .clk(clk));  // open: clr
  Register #(.width(16)) register_3 (.D(Din), .en(demultiplexer_1_out2), .Q(register_3_q), .clk(clk));  // open: clr
  Register #(.width(16)) register_4 (.D(Din), .en(demultiplexer_1_out3), .Q(register_4_q), .clk(clk));  // open: clr
  Multiplexer #(.select(2), .width(16), .enable("false")) multiplexer_1 (
    .in0(register_1_q), .in1(register_2_q), .in2(register_3_q), .in3(register_4_q), .out(D2), .sel(Ra0));
  Multiplexer #(.select(2), .width(16), .enable("false")) multiplexer_2 (
    .in0(register_1_q), .in1(register_2_q), .in2(register_3_q), .in3(register_4_q), .out(D1), .sel(Ra1));
endmodule

module _16b_Comparator (
  input  [15:0] A,
  input  [15:0] B,
  input  lt_in,
  input  eq_in,
  output lt_out,
  output eq_out
);

  wire n8b_comparator_1_eq_out, n8b_comparator_1_lt_out;

  _8b_Comparator u_8b_comparator_1 (
    .A(A[15:8]), .B(B[15:8]), .lt_in(lt_in), .eq_in(eq_in), .lt_out(n8b_comparator_1_lt_out),
    .eq_out(n8b_comparator_1_eq_out));
  _8b_Comparator u_8b_comparator_2 (
    .A(A[7:0]), .B(B[7:0]), .lt_in(n8b_comparator_1_lt_out), .eq_in(n8b_comparator_1_eq_out),
    .lt_out(lt_out), .eq_out(eq_out));
endmodule

module _8b_Comparator (
  input  [7:0] A,
  input  [7:0] B,
  input  lt_in,
  input  eq_in,
  output lt_out,
  output eq_out
);

  wire n4b_comparator_1_eq_out, n4b_comparator_1_lt_out;

  _4b_Comparator u_4b_comparator_1 (
    .A(A[7:4]), .B(B[7:4]), .lt_in(lt_in), .eq_in(eq_in), .lt_out(n4b_comparator_1_lt_out),
    .eq_out(n4b_comparator_1_eq_out));
  _4b_Comparator u_4b_comparator_2 (
    .A(A[3:0]), .B(B[3:0]), .lt_in(n4b_comparator_1_lt_out), .eq_in(n4b_comparator_1_eq_out),
    .lt_out(lt_out), .eq_out(eq_out));
endmodule

module _4b_Comparator (
  input  [3:0] A,
  input  [3:0] B,
  input  lt_in,
  input  eq_in,
  output lt_out,
  output eq_out
);

  wire n2b_comparator_1_eq_out, n2b_comparator_1_lt_out;

  _2b_Comparator u_2b_comparator_1 (
    .A(A[3:2]), .B(B[3:2]), .lt_in(lt_in), .eq_in(eq_in), .lt_out(n2b_comparator_1_lt_out),
    .eq_out(n2b_comparator_1_eq_out));
  _2b_Comparator u_2b_comparator_2 (
    .A(A[1:0]), .B(B[1:0]), .lt_in(n2b_comparator_1_lt_out), .eq_in(n2b_comparator_1_eq_out),
    .lt_out(lt_out), .eq_out(eq_out));
endmodule

module _2b_Comparator (
  input  [1:0] A,
  input  [1:0] B,
  input  lt_in,
  input  eq_in,
  output lt_out,
  output eq_out
);

  wire n1b_comparator_1_eq_out, n1b_comparator_1_lt_out;

  _1b_Comparator u_1b_comparator_1 (
    .lt_in(lt_in), .X(A[1]), .Y(B[1]), .eq_in(eq_in), .lt_out(n1b_comparator_1_lt_out),
    .eq_out(n1b_comparator_1_eq_out));
  _1b_Comparator u_1b_comparator_2 (
    .lt_in(n1b_comparator_1_lt_out), .X(A[0]), .Y(B[0]), .eq_in(n1b_comparator_1_eq_out), .lt_out(lt_out),
    .eq_out(eq_out));
endmodule

module _1b_Comparator (
  input  lt_in,
  input  X,
  input  Y,
  input  eq_in,
  output lt_out,
  output eq_out
);

  wire and_1_out, xnor_1_out;

  and and_1 (and_1_out, ~X, Y);  // AND_Gate
  xnor xnor_1 (xnor_1_out, X, Y);
  Multiplexer #(.enable("false")) multiplexer_1 (.in0(lt_in), .in1(and_1_out), .out(lt_out), .sel(eq_in));
  and and_2 (eq_out, xnor_1_out, eq_in);

  // Notes on the sheet:
  //   x < y
endmodule
